# Fritzing sketch circuit (saved by Fritzing 0.9.3b)

parts:
  Debugger1 = Debugger
  Espessif_Serial_Wifi_Modul_1 = ESP8266 ESP01 [part_number=ESP8266 package=THT]

nets:
  N1: Debugger1.3v, Espessif_Serial_Wifi_Modul_1.VCC, Espessif_Serial_Wifi_Modul_1.CH_PD
  GND: Debugger1.GND, Espessif_Serial_Wifi_Modul_1.GND
  N2: Debugger1.RX, Espessif_Serial_Wifi_Modul_1.TXD
  N3: Debugger1.TX, Espessif_Serial_Wifi_Modul_1.RXD

custom parts:
  ESP8266 ESP01: Generic WiFi Module based on the ESP8266 with onboard PCB antenna and UART communications
