# Fritzing sketch Sketch (saved by Fritzing 0.9.3b)
breadboards: 1

parts:
  Heltec_WiFi_LoRa_32_V1 = Heltec WiFi LoRa 32 V2 [part_number=HTIT-WB32LA]
  M1 = ph-4502c [package=THT]
  Componente1 = Adafruit ADS1115 16Bit I2C ADC [part_number="Adafruit #1085"]

nets:
  N1: Heltec_WiFi_LoRa_32_V1.pin_1, Componente1.SCL
  N2: Heltec_WiFi_LoRa_32_V1.pin_18, Heltec_WiFi_LoRa_32_V1.pin_19, M1.pin4, M1.pin5, Componente1.GND
  N3: Heltec_WiFi_LoRa_32_V1.pin_20, M1.pin6, Componente1.VDD
  N4: Heltec_WiFi_LoRa_32_V1.pin_27, Componente1.SDA
  N5: M1.pin3, Componente1.AIN0

notes:
  pino 22 = SCL
  pino 1 = SDA
  Nos docs do ADS, diz que ele pode ser alimentado de 2 a 5.4v. Testei este circuito, variando apenas a alimentação do ADS para 3.3v, porém a conversão ADC não fica a mesma. É importante calibrar o sensor de pH para uma tensão convencionada durante o projeto do circuito, para que as leituras do sensor não percam precisão.

custom parts:
  Heltec WiFi LoRa 32 V2: Heltec WiFi LoRa 32 V2 WiFi LoRa 32 is a classic IoT dev-board designed & produced by Heltec Automation(TM). It’s a highly integrated product based on ESP32 + SX127x, it has Wi-Fi, BLE, LoRa functions, also Li-Po battery management system, 0.96″ OLED are also included. It’s the best choice for smart cities, smart farms, smart home, and IoT makers.
  ph-4502c: ph-4502c PH Meter.
  Adafruit ADS1115 16Bit I2C ADC: For microcontrollers without an analog-to-digital converter or when you want a higher-precision ADC, the ADS1115 provides 16-bit precision at 860 samples/second over I2C. The chip can be configured as 4 single-ended input channels, or two differential channels. As a nice bonus, it even includes a programmable gain amplifier, up to x16, to help boost up smaller single/differential signals to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
