# Fritzing sketch Sketch (saved by Fritzing 0.9.3b)
breadboards: 1

parts:
  Heltec_WiFi_LoRa_32_V1 = Heltec WiFi LoRa 32 V2 [part_number=HTIT-WB32LA]
  DS1 = DS18B20 1-Wire Temperature Sensor [part_number=DS18B20]
  R3 = Resistor [tolerance=±5% resistance=4.7k package=THT]

nets:
  N1: Heltec_WiFi_LoRa_32_V1.pin_16, Heltec_WiFi_LoRa_32_V1.pin_17, DS1.VDD, R3.Pin_0
  N2: Heltec_WiFi_LoRa_32_V1.pin_18, Heltec_WiFi_LoRa_32_V1.pin_19, DS1.GND
  N3: Heltec_WiFi_LoRa_32_V1.pin_29, DS1.DQ, R3.Pin_1

notes:
  VDD - 3.3v
  GND - GND (0v)
  Pin Dados - VDD com Resistor 4.7k
  conectar o pino de dados do esp32 no pino de dados do sensor, antes do resistor.

custom parts:
  Heltec WiFi LoRa 32 V2: Heltec WiFi LoRa 32 V2 WiFi LoRa 32 is a classic IoT dev-board designed & produced by Heltec Automation(TM). It’s a highly integrated product based on ESP32 + SX127x, it has Wi-Fi, BLE, LoRa functions, also Li-Po battery management system, 0.96″ OLED are also included. It’s the best choice for smart cities, smart farms, smart home, and IoT makers.
